# Fritzing sketch shift-seven (saved by Fritzing 0.9.2b)
breadboards: 2

parts:
  Shift_Register = 74HC595 [package="DIP16 [THT]"]
  7_Segment1 = 7 Segment Display
  R3 = Resistor [tolerance=±5% resistance=330 package="2010 [SMD]"]
  R4 = Resistor [tolerance=±5% resistance=330 package="2010 [SMD]"]
  R5 = Resistor [tolerance=±5% resistance=330 package="2010 [SMD]"]
  R6 = Resistor [tolerance=±5% resistance=330 package="2010 [SMD]"]
  R7 = Resistor [tolerance=±5% resistance=330 package="2010 [SMD]"]
  R8 = Resistor [tolerance=±5% resistance=330 package="2010 [SMD]"]
  R9 = Resistor [tolerance=±5% resistance=330 package="2010 [SMD]"]
  Arudino = Arduino Uno (Rev3) - ICSP
  R10 = Resistor [tolerance=±5% resistance=330 package="2010 [SMD]"]

nets:
  N1: Shift_Register.Q1, R3.Pin_0
  N2: Shift_Register.Q2, R4.Pin_0
  N3: Shift_Register.Q3, R5.Pin_0
  N4: Shift_Register.Q4, R6.Pin_0
  N5: Shift_Register.Q5, R7.Pin_0
  N6: Shift_Register.Q6, R8.Pin_0
  N7: Shift_Register.Q7, R9.Pin_0
  GND: Shift_Register.GND, Shift_Register.OE, 7_Segment1.common_cathode, Arudino.GND
  VCC: Shift_Register.MR, Shift_Register.VCC, Arudino.5V
  N8: Shift_Register.SH_CP, Arudino.D3_PWM
  N9: Shift_Register.ST_CP, Arudino.D4
  N10: Shift_Register.DS, Arudino.D2
  N11: Shift_Register.Q0, R10.Pin_0
  N12: 7_Segment1.Segment_E, R6.Pin_1
  N13: 7_Segment1.Segment_D, R5.Pin_1
  N14: 7_Segment1.Segment_C, R4.Pin_1
  N15: 7_Segment1.Segment_DP, R9.Pin_1
  N16: 7_Segment1.Segment_B, R3.Pin_1
  N17: 7_Segment1.Segment_A, R10.Pin_1
  N18: 7_Segment1.Segment_F, R7.Pin_1
  N19: 7_Segment1.Segment_G, R8.Pin_1
